# Fritzing sketch circuit (saved by Fritzing 0.9.10b)
breadboards: 1

parts:
  LED3 = LED - 5mm [color="Red (633nm)" current=0.030 package="5 mm [THT]"]
  LED4 = LED - 5mm [color="Green (560nm)" current=0.030 package="5 mm [THT]"]
  J4 = Piezo Speaker
  BULB3 = Incandescent light bulb small [package="bulb sm"]
  BULB4 = Incandescent light bulb small [package="bulb sm"]
  J5 = 220v plug
  J6 = 120V duplex outlet_1
  KF-5 = KF-301 Relay [package=THT]
  KF-6 = KF-301 Relay [package=THT]
  KF-7 = KF-301 Relay [package=THT]
  KF-8 = KF-301 Relay [package=THT]
  Part1 = Arduino Uno (Rev3) - ICSP
  S1 = KY-026
  F1 = Fan - Ventilador [package=THT]
  J7 = Basic Servo
  Display1 = LCD screen 16x2 IIC [part_number=101290]

nets:
  N1: LED3.anode, Part1.D3_PWM
  GND: LED4.cathode, J4.pin1, Part1.GND, Display1.GND
  N2: LED4.anode, Part1.D4
  N3: J4.pin2, Part1.D5_PWM
  N4: BULB3.2, KF-7.NO
  N5: BULB4.2, KF-8.NO
  N6: J5.pin1, F1.GND
  N7: J6.N1, KF-5.NO
  N8: KF-5.signal, Part1.D11_PWM/MOSI
  N9: KF-6.signal, Part1.D12/MISO
  N10: KF-6.NC, F1.5V
  N11: KF-7.signal, Part1.D10_PWM/SS
  N12: KF-7.power, KF-8.power
  N13: KF-7.ground, KF-8.ground
  N14: KF-7.C, KF-8.C
  N15: KF-8.signal, Part1.D8
  N16: Part1.A4/SDA, Display1.SDA
  N17: Part1.A5/SCL, Display1.SCL
  N18: Part1.D6_PWM, S1.pin4
  N19: Part1.D7, J7.pulse
  5V: Part1.5V, Display1.VCC

custom parts:
  220v plug: Generic 220V AC plug.
  120V duplex outlet_1: 120V duplex outlet.
  KF-301 Relay: KF-301
  KY-026: ky-026 flame sensor module
  Fan - Ventilador: Ventilador de 2 pines, se encuentra comunmente en computadoras de escritorio
  LCD screen 16x2 IIC: LCD screen with HD44780 controller enables showing text, symbols, value or anything else that comes from Croduino/Arduino. It is capable of showing 16 symbols in two lines and therefore can be used in many projects that need to send clearly visible and legible output information.. • Color of symbols: White • Backlight: Blue • Dimensions: 80 x 36 x 12 mm • Screen dimensions: 64.5 x 16 mm •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
